// Logisim project RV32_single_R_I.circ as structural Verilog: 6 circuits, main circuit CPU
module CPU (
);

  wire BSel, CLK, isEqual, RegWEn, WBSel;
  wire [2:0] decode_1_funct3;
  wire [3:0] ALUSel;
  wire [4:0] decode_1_r1, decode_1_r2, decode_1_rd;
  wire [6:0] decode_1_funct7, decode_1_opcode;
  wire [11:0] decode_1_imm_11_0;
  wire [31:0] ALU_OUT, bit_extender_1_out, fetch_1_instruction, fetch_1_pc_out, multiplexer_1_out,
       ram_1_dout, registers_1_out_8, registers_1_outputs, RegWriteData;

  Clock clock_1 (.out(CLK));
  // Probe on decode_1_funct7
  // Probe on decode_1_funct3
  FETCH fetch_1 (.CLK(CLK), .Instruction(fetch_1_instruction), .PC_OUT(fetch_1_pc_out));  // open: PC_IN
  // Probe on fetch_1_pc_out
  // Probe on decode_1_opcode
  // Probe on fetch_1_instruction
  // Probe on decode_1_rd
  DECODE decode_1 (
    .Instruction(fetch_1_instruction), .Opcode(decode_1_opcode), .RD(decode_1_rd), .FUNCT3(decode_1_funct3),
    .R1(decode_1_r1), .R2(decode_1_r2), .FUNCT7(decode_1_funct7), .IMM_11_0(decode_1_imm_11_0));  // open: IMM_4_0, IMM_11_5
  CONTROL control_1 (
    .FUNCT3(decode_1_funct3), .FUNCT7(decode_1_funct7), .OPCODE(decode_1_opcode), .ALUSel(ALUSel),
    .RegWEn(RegWEn), .BSel(BSel), .WBSel(WBSel));
  // Probe on decode_1_r1
  REGISTERS registers_1 (
    .in_5(RegWEn), .in_6(CLK), .in_1(decode_1_r1), .in_2(decode_1_r2), .in_3(decode_1_rd),
    .in_4(RegWriteData), .Outputs(registers_1_outputs), .out_8(registers_1_out_8));
  // Probe on decode_1_imm_11_0
  assign bit_extender_1_out = {{20{decode_1_imm_11_0[11]}}, decode_1_imm_11_0};  // Bit_Extender bit_extender_1
  RAM #(.addrWidth(11), .dataWidth(32), .enables("line")) ram_1 (
    .addr(ALU_OUT[10:0]), .dout(ram_1_dout));  // open: we, clk, din
  // Probe on bit_extender_1_out
  // Probe on registers_1_outputs
  // Probe on registers_1_out_8
  Multiplexer #(.width(32)) multiplexer_1 (
    .in0(registers_1_out_8), .in1(bit_extender_1_out), .out(multiplexer_1_out), .sel(BSel));
  // Probe on ram_1_dout
  ALU alu_1 (.in_1(registers_1_outputs), .in_2(multiplexer_1_out), .in_3(ALUSel), .Outputs(ALU_OUT), .out_5(isEqual));
  // Probe on ALUSel
  // Probe on ALU_OUT
  Multiplexer #(.width(32)) multiplexer_2 (.in0(ALU_OUT), .in1(ram_1_dout), .out(RegWriteData), .sel(WBSel));

  // Notes on the sheet:
  //   ALU
endmodule

module REGISTERS (
  input  [4:0] in_1,
  input  [4:0] in_2,
  input  [4:0] in_3,
  input  [31:0] in_4,
  input  in_5,
  input  in_6,
  output [31:0] Outputs,
  output [31:0] out_8
);

  wire WE_1, WE_2, WE_3, WE_4, WE_5, WE_6, WE_7, WE_8, WE_9, WE_10, WE_11, WE_12, WE_13, WE_14, WE_15, WE_16,
       WE_17, WE_18, WE_19, WE_20, WE_21, WE_22, WE_23, WE_24, WE_25, WE_26, WE_27, WE_28, WE_29, WE_30,
       WE_31;
  wire [31:0] in_r1, in_r2, in_r3, in_r4, in_r5, in_r6, in_r7, in_r8, in_r9, in_r10, in_r11, in_r12, in_r13,
       in_r14, in_r15, in_r16, in_r17, in_r18, in_r19, in_r20, in_r21, in_r22, in_r23, in_r24, in_r25,
       in_r26, in_r27, in_r28, in_r29, in_r30, in_r31, out_r1, out_r2, out_r3, out_r4, out_r5, out_r6,
       out_r7, out_r8, out_r9, out_r10, out_r11, out_r12, out_r13, out_r14, out_r15, out_r16, out_r17,
       out_r18, out_r19, out_r20, out_r21, out_r22, out_r23, out_r24, out_r25, out_r26, out_r27, out_r28,
       out_r29, out_r30, out_r31;

  Register #(.width(32)) r1 (.D(in_r1), .en(WE_1), .clk(in_6), .Q(out_r1));  // open: clr
  Register #(.width(32)) register_1 (.D(in_r9), .en(WE_9), .clk(in_6), .Q(out_r9));  // open: clr
  Register #(.width(32)) register_2 (.D(in_r17), .en(WE_17), .clk(in_6), .Q(out_r17));  // open: clr
  Register #(.width(32)) register_3 (.D(in_r25), .en(WE_25), .clk(in_6), .Q(out_r25));  // open: clr
  Multiplexer #(.select(5), .width(32)) multiplexer_1 (
    .in0({32{1'b0}}), .in1(out_r1), .in2(out_r2), .in3(out_r3), .in4(out_r4), .in5(out_r5), .in6(out_r6),
    .in7(out_r7), .in8(out_r8), .in9(out_r9), .in10(out_r10), .in11(out_r11), .in12(out_r12), .in13(out_r13),
    .in14(out_r14), .in15(out_r15), .in16(out_r16), .in17(out_r17), .in18(out_r18), .in19(out_r19),
    .in20(out_r20), .in21(out_r21), .in22(out_r22), .in23(out_r23), .in24(out_r24), .in25(out_r25),
    .in26(out_r26), .in27(out_r27), .in28(out_r28), .in29(out_r29), .in30(out_r30), .in31(out_r31),
    .out(Outputs), .sel(in_1));
  Register #(.width(32)) register_4 (.D(in_r2), .en(WE_2), .clk(in_6), .Q(out_r2));  // open: clr
  Register #(.width(32)) register_5 (.D(in_r10), .en(WE_10), .clk(in_6), .Q(out_r10));  // open: clr
  Register #(.width(32)) register_6 (.D(in_r18), .en(WE_18), .clk(in_6), .Q(out_r18));  // open: clr
  Register #(.width(32)) register_7 (.D(in_r26), .en(WE_26), .clk(in_6), .Q(out_r26));  // open: clr
  Register #(.width(32)) register_8 (.D(in_r3), .en(WE_3), .clk(in_6), .Q(out_r3));  // open: clr
  Register #(.width(32)) register_9 (.D(in_r11), .en(WE_11), .clk(in_6), .Q(out_r11));  // open: clr
  Register #(.width(32)) register_10 (.D(in_r19), .en(WE_19), .clk(in_6), .Q(out_r19));  // open: clr
  Register #(.width(32)) register_11 (.D(in_r27), .en(WE_27), .clk(in_6), .Q(out_r27));  // open: clr
  Multiplexer #(.select(5), .width(32)) multiplexer_2 (
    .in0({32{1'b0}}), .in1(out_r1), .in2(out_r2), .in3(out_r3), .in4(out_r4), .in5(out_r5), .in6(out_r6),
    .in7(out_r7), .in8(out_r8), .in9(out_r9), .in10(out_r10), .in11(out_r11), .in12(out_r12), .in13(out_r13),
    .in14(out_r14), .in15(out_r15), .in16(out_r16), .in17(out_r17), .in18(out_r18), .in19(out_r19),
    .in20(out_r20), .in21(out_r21), .in22(out_r22), .in23(out_r23), .in24(out_r24), .in25(out_r25),
    .in26(out_r26), .in27(out_r27), .in28(out_r28), .in29(out_r29), .in30(out_r30), .in31(out_r31),
    .out(out_8), .sel(in_2));
  Register #(.width(32)) register_12 (.D(in_r4), .en(WE_4), .clk(in_6), .Q(out_r4));  // open: clr
  Register #(.width(32)) register_13 (.D(in_r12), .en(WE_12), .clk(in_6), .Q(out_r12));  // open: clr
  Register #(.width(32)) register_14 (.D(in_r20), .en(WE_20), .clk(in_6), .Q(out_r20));  // open: clr
  Register #(.width(32)) register_15 (.D(in_r28), .en(WE_28), .clk(in_6), .Q(out_r28));  // open: clr
  Demultiplexer #(.enable("true"), .select(5), .width(32)) demultiplexer_1 (
    .out1(in_r1), .out2(in_r2), .out3(in_r3), .out4(in_r4), .out5(in_r5), .out6(in_r6), .out7(in_r7),
    .out8(in_r8), .out9(in_r9), .out10(in_r10), .out11(in_r11), .out12(in_r12), .out13(in_r13),
    .out14(in_r14), .out15(in_r15), .out16(in_r16), .out17(in_r17), .out18(in_r18), .out19(in_r19),
    .out20(in_r20), .out21(in_r21), .out22(in_r22), .out23(in_r23), .out24(in_r24), .out25(in_r25),
    .out26(in_r26), .out27(in_r27), .out28(in_r28), .out29(in_r29), .out30(in_r30), .out31(in_r31),
    .in(in_4), .sel(in_3), .en(in_5));  // open: out0
  Register #(.width(32)) register_16 (.D(in_r5), .en(WE_5), .clk(in_6), .Q(out_r5));  // open: clr
  Register #(.width(32)) register_17 (.D(in_r13), .en(WE_13), .clk(in_6), .Q(out_r13));  // open: clr
  Register #(.width(32)) register_18 (.D(in_r21), .en(WE_21), .clk(in_6), .Q(out_r21));  // open: clr
  Register #(.width(32)) register_19 (.D(in_r29), .en(WE_29), .clk(in_6), .Q(out_r29));  // open: clr
  Register #(.width(32)) register_20 (.D(in_r6), .en(WE_6), .clk(in_6), .Q(out_r6));  // open: clr
  Register #(.width(32)) register_21 (.D(in_r14), .en(WE_14), .clk(in_6), .Q(out_r14));  // open: clr
  Register #(.width(32)) register_22 (.D(in_r22), .en(WE_22), .clk(in_6), .Q(out_r22));  // open: clr
  Register #(.width(32)) register_23 (.D(in_r30), .en(WE_30), .clk(in_6), .Q(out_r30));  // open: clr
  Decoder #(.select(5)) decoder_1 (
    .out1(WE_1), .out2(WE_2), .out3(WE_3), .out4(WE_4), .out5(WE_5), .out6(WE_6), .out7(WE_7), .out8(WE_8),
    .out9(WE_9), .out10(WE_10), .out11(WE_11), .out12(WE_12), .out13(WE_13), .out14(WE_14), .out15(WE_15),
    .out16(WE_16), .out17(WE_17), .out18(WE_18), .out19(WE_19), .out20(WE_20), .out21(WE_21), .out22(WE_22),
    .out23(WE_23), .out24(WE_24), .out25(WE_25), .out26(WE_26), .out27(WE_27), .out28(WE_28), .out29(WE_29),
    .out30(WE_30), .out31(WE_31), .sel(in_3), .en(in_5));  // open: out0
  Register #(.width(32)) register_24 (.D(in_r7), .en(WE_7), .clk(in_6), .Q(out_r7));  // open: clr
  Register #(.width(32)) register_25 (.D(in_r15), .en(WE_15), .clk(in_6), .Q(out_r15));  // open: clr
  Register #(.width(32)) register_26 (.D(in_r23), .en(WE_23), .clk(in_6), .Q(out_r23));  // open: clr
  Register #(.width(32)) register_27 (.D(in_r31), .en(WE_31), .clk(in_6), .Q(out_r31));  // open: clr
  Register #(.width(32)) register_28 (.D(in_r8), .en(WE_8), .clk(in_6), .Q(out_r8));  // open: clr
  Register #(.width(32)) register_29 (.D(in_r16), .en(WE_16), .clk(in_6), .Q(out_r16));  // open: clr
  Register #(.width(32)) register_30 (.D(in_r24), .en(WE_24), .clk(in_6), .Q(out_r24));  // open: clr

  // Other names for the same wires on the sheet: CLK = in_6; reg1[4:0] = in_1; reg1_data[31:0] = Outputs;
  //   reg2[4:0] = in_2; reg2_data[31:0] = out_8; reg_write[4:0] = in_3; reg_write_data[31:0] = in_4; WE = in_5

  // Notes on the sheet:
  //   I/O
  //   Inputs
  //   Register Reading
  //   Register Writing
endmodule

module ALU (
  input  [31:0] in_1,
  input  [31:0] in_2,
  input  [3:0] in_3,
  output [31:0] Outputs,
  output out_5
);

  wire comparator_1_lt;
  wire [31:0] o_add, o_and, o_div, o_mul, o_mulh, o_or, o_rem, o_sll, o_slt, o_srl, o_sub, o_xor;

  Multiplexer #(.select(4), .width(32)) multiplexer_1 (
    .in0(o_add), .in1(o_sub), .in2(o_and), .in3(o_or), .in4(o_xor), .in5(o_sll), .in6(o_srl), .in7(o_mul),
    .in8(o_mulh), .in9(o_div), .in10(o_rem), .in11(o_slt), .out(Outputs), .sel(in_3));  // open: in12, in13, in14, in15
  Adder #(.width(32)) adder_1 (.a(in_1), .b(in_2), .out(o_add));  // open: cin, cout
  Subtractor #(.width(32)) subtractor_1 (.a(in_1), .b(in_2), .out(o_sub));  // open: bin, bout
  assign o_and = in_1 & in_2;  // AND_Gate and_1, 32 bits wide
  assign o_or = in_1 | in_2;  // OR_Gate or_1, 32 bits wide
  assign o_xor = in_1 ^ in_2;  // XOR_Gate xor_1, 32 bits wide
  Shifter #(.width(32)) shifter_1 (.in(in_1), .\dist (in_2[4:0]), .out(o_sll));
  Comparator #(.width(32)) comparator_1 (.a(in_1), .b(in_2), .lt(comparator_1_lt));  // open: gt, eq
  Shifter #(.shift("lr"), .width(32)) shifter_2 (.in(in_1), .\dist (in_2[4:0]), .out(o_srl));
  Multiplier #(.width(32)) multiplier_1 (.a(in_1), .b(in_2), .out(o_mul));  // open: cin, cout
  Multiplier #(.width(32)) multiplier_2 (.a(in_1), .b(in_2), .cout(o_mulh));  // open: out, cin
  Divider #(.width(32)) divider_1 (.a(in_1), .b(in_2), .out(o_div));  // open: upper, rem
  Divider #(.width(32)) divider_2 (.a(in_1), .b(in_2), .rem(o_rem));  // open: out, upper
  Comparator #(.width(32)) comparator_2 (.a(in_1), .b(in_2), .eq(out_5));  // open: gt, lt
  Bit_Extender #(.in_width(1), .out_width(32)) bit_extender_1 (.out(o_slt));  // open: in

  // Other names for the same wires on the sheet: isEqual = out_5; OP[3:0] = in_3; result[31:0] = Outputs;
  //   X[31:0] = in_1; Y[31:0] = in_2

  // Notes on the sheet:
  //   I/O
  //   Operation Selection
  //   Inputs
  //   Operations
endmodule

module FETCH (
  input  [31:0] PC_IN,
  input  CLK,
  output [31:0] Instruction,
  output [31:0] PC_OUT
);

  wire [31:0] adder_1_out;

  ROM #(.addrWidth(10), .dataWidth(32)) rom_1 (.addr(PC_OUT[9:0]), .data(Instruction));
  Adder #(.width(32)) adder_1 (.a(PC_OUT), .b(32'h1), .out(adder_1_out));  // open: cin, cout
  Register #(.width(32)) register_1 (.D(adder_1_out), .clk(CLK), .Q(PC_OUT));  // open: en, clr
  // Probe on PC_OUT
  // Probe on Instruction

  // Other names for the same wires on the sheet: PC[31:0] = PC_OUT

  // Notes on the sheet:
  //   contents of rom_1 (hex, n*v repeats v):
  //   cc00913 ff00993 1394a33 cc94a93
endmodule

module DECODE (
  input  [31:0] Instruction,
  output [6:0] Opcode,
  output [4:0] RD,
  output [2:0] FUNCT3,
  output [4:0] R1,
  output [4:0] R2,
  output [6:0] FUNCT7,
  output [11:0] IMM_11_0,
  output [4:0] IMM_4_0,
  output [6:0] IMM_11_5
);


  assign FUNCT3 = Instruction[14:12];
  assign FUNCT7 = Instruction[31:25];
  assign IMM_4_0 = Instruction[11:7];
  assign IMM_11_0 = Instruction[31:20];
  assign IMM_11_5 = Instruction[31:25];
  assign Opcode = Instruction[6:0];
  assign R1 = Instruction[19:15];
  assign R2 = Instruction[24:20];
  assign RD = Instruction[11:7];

  // Notes on the sheet:
  //   R-Type
  //   I-Type
  //   S-Type
endmodule

module CONTROL (
  input  [2:0] FUNCT3,
  input  [6:0] FUNCT7,
  input  [6:0] OPCODE,
  output [3:0] ALUSel,
  output RegWEn,
  output BSel,
  output WBSel
);

  wire comparator_4_eq, comparator_5_eq, comparator_6_eq, comparator_7_eq, comparator_8_eq, comparator_9_eq,
       comparator_10_eq, comparator_11_eq, comparator_12_eq, comparator_13_eq, comparator_14_eq,
       comparator_15_eq, comparator_16_eq, comparator_17_eq, comparator_18_eq, comparator_19_eq,
       comparator_20_eq, comparator_21_eq, I_add, I_and, I_or, I_sll, I_TYPE_LOAD, I_TYPE_OTHER, I_xor,
       or_1_out, or_2_out, or_3_out, or_4_out, or_5_out, R_add, R_and, R_or, R_sll, R_sub, R_xor, undriven,
       undriven_2, undriven_3, undriven_4, undriven_5, undriven_6;

  or or_1 (or_1_out, R_and, I_and);
  or or_2 (or_2_out, R_or, I_or);
  or or_3 (or_3_out, R_xor, I_xor);
  or or_4 (or_4_out, R_sll, I_sll);
  or or_5 (or_5_out, R_add, I_TYPE_LOAD, I_add);
  Comparator #(.width(7)) comparator_1 (.a(OPCODE), .b(7'b0110011), .eq(WBSel));  // open: gt, lt
  Comparator #(.width(7)) comparator_2 (.a(OPCODE), .b(7'b0010011), .eq(I_TYPE_OTHER));  // open: gt, lt
  Comparator #(.width(7)) comparator_3 (.a(OPCODE), .b(7'b0000011), .eq(I_TYPE_LOAD));  // open: gt, lt
  Priority_Encoder #(.select(4)) priority_encoder_1 (
    .in0(or_5_out), .in1(R_sub), .in2(or_1_out), .in3(or_2_out), .in4(or_3_out), .in5(or_4_out),
    .in6(undriven), .in7(undriven_2), .in8(undriven_3), .in9(undriven_4), .in10(undriven_5),
    .in11(undriven_6), .out(ALUSel));  // open: in12, in13, in14, in15, gs, en_out, en_in
  buf or_6 (RegWEn, I_TYPE_LOAD);  // OR_Gate
  or or_7 (BSel, I_TYPE_LOAD, I_TYPE_OTHER);
  Comparator #(.width(3)) comparator_4 (.a(FUNCT3), .b(3'b000), .eq(comparator_4_eq));  // open: gt, lt
  Comparator #(.width(7)) comparator_5 (.a(FUNCT7), .b({7{1'b0}}), .eq(comparator_5_eq));  // open: gt, lt
  Comparator #(.width(3)) comparator_6 (.a(FUNCT3), .b(3'b000), .eq(comparator_6_eq));  // open: gt, lt
  Comparator #(.width(7)) comparator_7 (.a(FUNCT7), .b(7'b0100000), .eq(comparator_7_eq));  // open: gt, lt
  Comparator #(.width(3)) comparator_8 (.a(FUNCT3), .b(3'b001), .eq(comparator_8_eq));  // open: gt, lt
  Comparator #(.width(7)) comparator_9 (.a(FUNCT7), .b({7{1'b0}}), .eq(comparator_9_eq));  // open: gt, lt
  Comparator #(.width(3)) comparator_10 (.a(FUNCT3), .b(3'b111), .eq(comparator_10_eq));  // open: gt, lt
  Comparator #(.width(7)) comparator_11 (.a(FUNCT7), .b({7{1'b0}}), .eq(comparator_11_eq));  // open: gt, lt
  Comparator #(.width(3)) comparator_12 (.a(FUNCT3), .b(3'b110), .eq(comparator_12_eq));  // open: gt, lt
  Comparator #(.width(7)) comparator_13 (.a(FUNCT7), .b({7{1'b0}}), .eq(comparator_13_eq));  // open: gt, lt
  Comparator #(.width(3)) comparator_14 (.a(FUNCT3), .b(3'b101), .eq(comparator_14_eq));  // open: gt, lt
  Comparator #(.width(7)) comparator_15 (.a(FUNCT7), .b({7{1'b0}}), .eq(comparator_15_eq));  // open: gt, lt
  Comparator #(.width(3)) comparator_16 (.a(FUNCT3), .b(3'b000), .eq(comparator_16_eq));  // open: gt, lt
  Comparator #(.width(3)) comparator_17 (.a(FUNCT3), .b(3'b001), .eq(comparator_17_eq));  // open: gt, lt
  Comparator #(.width(7)) comparator_18 (.a(FUNCT7), .b({7{1'b0}}), .eq(comparator_18_eq));  // open: gt, lt
  Comparator #(.width(3)) comparator_19 (.a(FUNCT3), .b(3'b111), .eq(comparator_19_eq));  // open: gt, lt
  Comparator #(.width(3)) comparator_20 (.a(FUNCT3), .b(3'b110), .eq(comparator_20_eq));  // open: gt, lt
  Comparator #(.width(3)) comparator_21 (.a(FUNCT3), .b(3'b110), .eq(comparator_21_eq));  // open: gt, lt
  and and_1 (R_add, WBSel, comparator_4_eq, comparator_5_eq);
  and and_2 (R_sub, WBSel, comparator_6_eq, comparator_7_eq);
  and and_3 (R_sll, WBSel, comparator_8_eq, comparator_9_eq);
  and and_4 (R_and, WBSel, comparator_10_eq, comparator_11_eq);
  and and_5 (R_or, WBSel, comparator_12_eq, comparator_13_eq);
  and and_6 (R_xor, WBSel, comparator_14_eq, comparator_15_eq);
  and and_7 (I_sll, I_TYPE_OTHER, comparator_17_eq, comparator_18_eq);
  and and_8 (I_add, I_TYPE_OTHER, comparator_16_eq);
  and and_9 (I_and, I_TYPE_OTHER, comparator_19_eq);
  and and_10 (I_or, I_TYPE_OTHER, comparator_20_eq);
  and and_11 (I_xor, I_TYPE_OTHER, comparator_21_eq);

  // Other names for the same wires on the sheet: R_TYPE = WBSel
endmodule
